# Fritzing sketch vfd-display (saved by Fritzing 0.9.10b)
circuit board: 20.3317cm x 6.85cm
breadboards: 1

parts:
  ULN2803A = ULN2803A [package=THT]
  10K = IC, SIP package, 9 pins [chip_label=IC]
  10K_2 = IC, SIP package, 9 pins [chip_label=IC]
  ULN2803A_2 = ULN2803A [package=THT]
  10K_3 = IC, SIP package, 9 pins [chip_label=IC]
  ULN2803A_3 = ULN2803A [package=THT]
  10K_4 = IC, SIP package, 9 pins [chip_label=IC]
  J1 = female pin header, 37 pins [form="♀ (female)"]
  MCP23008 = IC, DIP package, 18 pins [chip_label=IC]
  MCP23008_2 = IC, DIP package, 18 pins [chip_label=IC]
  MCP23008_3 = IC, DIP package, 18 pins [chip_label=IC]
  ULN2803A_4 = ULN2803A [package=THT]
  MCP23008_4 = IC, DIP package, 18 pins [chip_label=IC]
  J2 = female pin header, 5 pins [form="♀ (female)"]
  J3 = female pin header, 5 pins [form="♀ (female)"]
  C2 = Electrolytic Capacitor [capacitance=1µF voltage=35V package="100 mil [THT, electrolytic]"]
  C1 = Electrolytic Capacitor [capacitance=1µF voltage=35V package="100 mil [THT, electrolytic]"]
  LD33V = Voltage Regulator [package=to220-adj]
  R1 = Resistor [tolerance=±5% power=0.25 resistance=220 package=THT]
  J1_2 = female pin header, 2 pins [form="♀ (female)"]

nets:
  N1: ULN2803A.In_1, MCP23008_4.pin17
  N2: ULN2803A.In_2, MCP23008_4.pin16
  N3: ULN2803A.In_3, MCP23008_4.pin15
  N4: ULN2803A.In_4, MCP23008_4.pin14
  N5: ULN2803A.In_5, MCP23008_4.pin13
  N6: ULN2803A.In_6, MCP23008_4.pin12
  N7: ULN2803A.In_7, MCP23008_4.pin11
  N8: ULN2803A.In_8, MCP23008_4.pin10
  N9: ULN2803A.0V, ULN2803A_2.0V, ULN2803A_3.0V, MCP23008.pin3, MCP23008.pin9, MCP23008_2.pin3, MCP23008_2.pin5, MCP23008_2.pin9, MCP23008_3.pin3, MCP23008_3.pin4, MCP23008_3.pin9, ULN2803A_4.0V, MCP23008_4.pin3, MCP23008_4.pin4, MCP23008_4.pin5, MCP23008_4.pin9, J2.pin4, J3.pin4, C2.-, C1.-, LD33V.ADJ, R1.Pin_0, J1_2.pin2
  N10: ULN2803A.COM_-_Common, 10K.pin1, 10K_2.pin1, ULN2803A_2.COM_-_Common, 10K_3.pin1, ULN2803A_3.COM_-_Common, 10K_4.pin1, ULN2803A_4.COM_-_Common, J1_2.pin1
  N11: ULN2803A.Out_8, 10K.pin9, J1.pin20
  N12: ULN2803A.Out_7, 10K.pin8, J1.pin22
  N13: ULN2803A.Out_6, 10K.pin7, J1.pin24
  N14: ULN2803A.Out_5, 10K.pin6, J1.pin27
  N15: ULN2803A.Out_4, 10K.pin5, J1.pin29
  N16: ULN2803A.Out_3, 10K.pin4, J1.pin31
  N17: ULN2803A.Out_2, 10K.pin3, J1.pin33
  N18: ULN2803A.Out_1, 10K.pin2, J1.pin35
  N19: 10K_2.pin2, J1.pin36, ULN2803A_4.Out_1
  N20: 10K_2.pin3, J1.pin34, ULN2803A_4.Out_2
  N21: 10K_2.pin4, J1.pin32, ULN2803A_4.Out_3
  N22: 10K_2.pin5, J1.pin30, ULN2803A_4.Out_4
  N23: 10K_2.pin6, J1.pin28, ULN2803A_4.Out_5
  N24: 10K_2.pin7, J1.pin26, ULN2803A_4.Out_6
  N25: 10K_2.pin8, J1.pin25, ULN2803A_4.Out_7
  N26: 10K_2.pin9, J1.pin23, ULN2803A_4.Out_8
  N27: ULN2803A_2.In_1, MCP23008_2.pin17
  N28: ULN2803A_2.In_2, MCP23008_2.pin16
  N29: ULN2803A_2.In_3, MCP23008_2.pin15
  N30: ULN2803A_2.In_4, MCP23008_2.pin14
  N31: ULN2803A_2.In_5, MCP23008_2.pin13
  N32: ULN2803A_2.In_6, MCP23008_2.pin12
  N33: ULN2803A_2.In_7, MCP23008_2.pin11
  N34: ULN2803A_2.In_8, MCP23008_2.pin10
  N35: ULN2803A_2.Out_8, 10K_3.pin9, J1.pin2
  N36: ULN2803A_2.Out_7, 10K_3.pin8, J1.pin6
  N37: ULN2803A_2.Out_6, 10K_3.pin7, J1.pin8
  N38: ULN2803A_2.Out_5, 10K_3.pin6, J1.pin10
  N39: ULN2803A_2.Out_4, 10K_3.pin5, J1.pin12
  N40: ULN2803A_2.Out_3, 10K_3.pin4, J1.pin13
  N41: ULN2803A_2.Out_2, 10K_3.pin3, J1.pin15
  N42: ULN2803A_2.Out_1, 10K_3.pin2, J1.pin17
  N43: ULN2803A_3.In_1, MCP23008.pin17
  N44: ULN2803A_3.In_2, MCP23008.pin16
  N45: ULN2803A_3.In_3, MCP23008.pin15
  N46: ULN2803A_3.In_4, MCP23008.pin14
  N47: ULN2803A_3.In_5, MCP23008.pin13
  N48: ULN2803A_3.In_6, MCP23008.pin12
  N49: ULN2803A_3.In_7, MCP23008.pin11
  N50: ULN2803A_3.In_8, MCP23008.pin10
  N51: ULN2803A_3.Out_8, 10K_4.pin9, J1.pin3
  N52: ULN2803A_3.Out_7, 10K_4.pin8, J1.pin5
  N53: ULN2803A_3.Out_6, 10K_4.pin7, J1.pin7
  N54: ULN2803A_3.Out_5, 10K_4.pin6, J1.pin9
  N55: ULN2803A_3.Out_4, 10K_4.pin5, J1.pin11
  N56: ULN2803A_3.Out_3, 10K_4.pin4, J1.pin14
  N57: ULN2803A_3.Out_2, 10K_4.pin3, J1.pin16
  N58: ULN2803A_3.Out_1, 10K_4.pin2, J1.pin18
  N59: J1.pin1, R1.Pin_1
  N60: J1.pin37, C2.+, LD33V.OUT
  N61: MCP23008.pin1, MCP23008_2.pin1, MCP23008_3.pin1, MCP23008_4.pin1, J2.pin2, J3.pin2
  N62: MCP23008.pin2, MCP23008_2.pin2, MCP23008_3.pin2, MCP23008_4.pin2, J2.pin1, J3.pin1
  N63: MCP23008.pin4, MCP23008.pin5, MCP23008.pin18, MCP23008_2.pin4, MCP23008_2.pin18, MCP23008_3.pin5, MCP23008_3.pin18, MCP23008_4.pin18, J2.pin3, J3.pin3, C1.+, LD33V.IN
  N64: MCP23008.pin6, MCP23008_2.pin6, MCP23008_3.pin6, MCP23008_4.pin6, J2.pin5, J3.pin5
  N65: MCP23008_3.pin10, ULN2803A_4.In_8
  N66: MCP23008_3.pin11, ULN2803A_4.In_7
  N67: MCP23008_3.pin12, ULN2803A_4.In_6
  N68: MCP23008_3.pin13, ULN2803A_4.In_5
  N69: MCP23008_3.pin14, ULN2803A_4.In_4
  N70: MCP23008_3.pin15, ULN2803A_4.In_3
  N71: MCP23008_3.pin16, ULN2803A_4.In_2
  N72: MCP23008_3.pin17, ULN2803A_4.In_1

notes:
  SDA
  SCL
  5V
  GND
  /RESET
  VFD Display Control V1
  (C) 2022 D. Thain
  30V
  000
  001
  010
  011
